# Fritzing sketch lightsaber (saved by Fritzing 1.0.6)
breadboards: 1

parts:
  U1 = Arduino Nano (Rev3.0)
  U2 = ADXL345 [package=lga14]

nets:
  GND: U1.GND, U2.GND, U2.VSS, U2.SDO
  N1: U1.D2, U2.INT1
  N2: U1.A5, U2.SCL
  N3: U1.A4, U2.SDA
  3V3: U1.3V3, U2.VDD, U2.CS
